// Digital circuit InstructionDecoder.dig as structural Verilog
// The InstructionDecoder component, which serves as a hub to control many of the signals to other components. It implements both the fetch operation, and execution of machine code (including decoding).
module InstructionDecoder (
  input  [31:0] Instruction,
  input  Fetch,
  input  Execute,
  output [3:0] Condition,
  output Halt,
  output [3:0] Reg_dest,
  output [3:0] Reg_B,
  output [3:0] Reg_A,
  output [2:0] Opcode,
  output nRE,
  output nWE,
  output Constant,
  output SetFlags,
  output UseConstant
);

  // InstructionSplitter instructionsplitter_1: pin names not known; wires that end beside it: Instruction
  // InstructionLOADHI instructionloadhi_1: pin names not known; wires that end beside it: Instruction
  InstructionPOP instructionpop_1 (.Instruction(Instruction));  // open: Reg_dest
  InstructionPUSH instructionpush_1 (.Instruction(Instruction));  // open: Reg_A
  // InstructionWRITE instructionwrite_1: pin names not known; wires that end beside it: Instruction
  // InstructionREAD instructionread_1: pin names not known; wires that end beside it: Instruction
  AllBits1 allbits1_1 (.Instruction_NoCond(Instruction[31:4]), .AllBits1(Halt));

  assign Condition = Instruction[3:0];

  // Notes on the sheet:
  //   Instruction: The instruction machine code input. If the CPU is in the fetch phase and a rising clock signal occurs, this machine code is stored in the internal instruction register (IR), so that it can be decoded and executed.
  //   Condition: Instruction condition output, which contains the condition under which the instruction should be executed.
  //   Reg_dest: Destination register output, which determines the register that should store the result of a data operation. A data operation is either an ALU computation, or a read from an external device, such as RAM.
  //   Reg_B: B register output, which determines the register to be used for the second operand.
  //   Reg_A: A register output, which determines the register to be used for the first operand.
  //   Opcode: Opcode output, which determines the operation the ALU should perform.
endmodule
